// Logisim project s-mips.circ as structural Verilog
module S_MIPS_Board (
  input  DESHABILITAR_DISPATCHER,
  output halt
);

  wire button_1_out, CLK, CS, d_ff_1_q, LCLR, LoadRAM, LoadRAMOn, LW, R_R_W, R_W, ram_dispatcher_1_finished,
       RCS, Reset_out, RST, TTY_EN;
  wire [2:0] KDB;
  wire [3:0] LMask, Mask, ram_1_read_time, ram_1_write_time, RMask;
  wire [6:0] KDB_DATA, TTY_DATA;
  wire [15:0] Addr, LAddr, RAddr;
  wire [31:0] I0, I1, I2, I3, LData, ram_1_data_out_0, ram_1_data_out_1, ram_1_data_out_2, ram_1_data_out_3,
       RI0, RI1, RI2, RI3;

  TTY #(.rows(25), .cols(80)) tty_1 (.data(TTY_DATA), .clk(CLK), .we(TTY_EN), .clr(RST));
  not not_1 (LoadRAMOn, ram_dispatcher_1_finished);
  RAM_Dispatcher ram_dispatcher_1 (
    .WriteTime(ram_1_write_time), .Clock(CLK), .Data(LData), .Address(LAddr), .Mask(LMask),
    .Finished(ram_dispatcher_1_finished), .Write(LW), .CLR(LCLR));
  Keyboard #(.buflen(64)) keyboard_1 (.clk(CLK), .re(KDB[0]), .avail(KDB[2]), .data(KDB_DATA));  // open: clr
  RAM_2 ram_1 (
    .Address(RAddr), .Data_Out_0(ram_1_data_out_0), .Data_Out_1(ram_1_data_out_1),
    .Data_Out_2(ram_1_data_out_2), .Data_Out_3(ram_1_data_out_3), .Data_In_0(RI0), .Data_In_1(RI1),
    .Data_In_2(RI2), .Data_In_3(RI3), .Mask(RMask), .nRead_Write(R_R_W), .Chip_Select(RCS),
    .Read_Time(ram_1_read_time), .Reset(button_1_out), .Write_Time(ram_1_write_time));
  Button button_1 (.out(button_1_out));
  D_Flip_Flop d_ff_1 (.clk(CLK), .D(1'b1), .Q(d_ff_1_q), .reset(Reset_out));  // open: Qn, preset, en
  Button Reset (.out(Reset_out));
  S_MIPS s_mips_1 (
    .Kbd_Enable(KDB[0]), .Address(Addr), .Kbd_Clear(KDB[1]), .Kbd_Available(KDB[2]), .RAM_In_0(I0),
    .Kbd_ASCII_Data(KDB_DATA), .RAM_In_1(I1), .TTY_Enable(TTY_EN), .RAM_In_2(I2), .RAM_In_3(I3),
    .TTY_ASCII_Data(TTY_DATA), .Reset(RST), .RAM_Out_0(ram_1_data_out_0), .Clock(CLK),
    .RAM_Out_1(ram_1_data_out_1), .Stop(halt), .RAM_Out_2(ram_1_data_out_2), .RAM_Out_3(ram_1_data_out_3),
    .Mask(Mask), .Read_Time(ram_1_read_time), .Write_Time(ram_1_write_time), .nRead_Write(R_W),
    .Chip_Select(CS));
  D_Flip_Flop d_ff_2 (.clk(CLK), .D(d_ff_1_q), .Qn(LCLR), .reset(Reset_out));  // open: Q, preset, en
  or or_1 (RST, LCLR, LoadRAM);
  Clock clock_1 (.out(CLK));
  Multiplexer #(.width(32), .enable("false")) multiplexer_1 (.in0(I0), .in1(LData), .out(RI0), .sel(LoadRAM));
  Multiplexer #(.width(32), .enable("false")) multiplexer_2 (.in0(I1), .in1(LData), .out(RI1), .sel(LoadRAM));
  Multiplexer #(.width(32), .enable("false")) multiplexer_3 (.in0(I2), .in1(LData), .out(RI2), .sel(LoadRAM));
  Multiplexer #(.width(32), .enable("false")) multiplexer_4 (.in0(I3), .in1(LData), .out(RI3), .sel(LoadRAM));
  and and_1 (LoadRAM, ~DESHABILITAR_DISPATCHER, LoadRAMOn);  // AND_Gate
  Multiplexer #(.width(16), .enable("false")) multiplexer_5 (.in0(Addr), .in1(LAddr), .out(RAddr), .sel(LoadRAM));
  Multiplexer #(.width(4), .enable("false")) multiplexer_6 (.in0(Mask), .in1(LMask), .out(RMask), .sel(LoadRAM));
  Multiplexer #(.enable("false")) multiplexer_7 (.in0(CS), .in1(LW), .out(RCS), .sel(LoadRAM));
  Multiplexer #(.enable("false")) multiplexer_8 (.in0(R_W), .in1(LW), .out(R_R_W), .sel(LoadRAM));

  // Notes on the sheet:
  //   NO MODIFICAR
  //   Keyboard
endmodule

module S_MIPS (
  input  Kbd_Available,
  input  [6:0] Kbd_ASCII_Data,
  input  [31:0] RAM_Out_0,
  input  [31:0] RAM_Out_1,
  input  Reset,
  input  [31:0] RAM_Out_2,
  input  Clock,
  input  [31:0] RAM_Out_3,
  input  [3:0] Read_Time,
  input  [3:0] Write_Time,
  output Kbd_Enable,
  output [15:0] Address,
  output Kbd_Clear,
  output TTY_Enable,
  output [6:0] TTY_ASCII_Data,
  output Stop,
  output [31:0] RAM_In_0,
  output [31:0] RAM_In_1,
  output [31:0] RAM_In_2,
  output [31:0] RAM_In_3,
  output [3:0] Mask,
  output nRead_Write,
  output Chip_Select
);

  wire Exec, fetch, halt, is_write, Load_i, MC_end, mem_needed, pop, PopLoad, push, PushLoad, r_w, start_mc;
  wire [31:0] Data_Read, Instruction, mem_address, mem_write_Data, PC;

  DATA_PATH data_path_1 (
    .Clock(Clock), .Reset(Reset), .Load_I(Load_i), .Execute_i(Exec), .Instruction_in(Instruction),
    .Data_in(Data_Read), .KBD_data(Kbd_ASCII_Data), .KBD_avail(Kbd_Available), .PC_out(PC),
    .mem_address(mem_address), .mem_write_data(mem_write_Data), .Halt(halt), .Memory_neede(mem_needed),
    .is_write(is_write), .TTY_data(TTY_ASCII_Data), .TTY_enable(TTY_Enable), .Push(push), .Pop(pop),
    .KBD_Enable(Kbd_Enable), .PushLoad(PushLoad), .PopLoad(PopLoad));
  // Control_Unit control_unit_1: pin names not known; wires that end beside it: halt, mem_needed, is_write, push, pop, MC_end, Clock, Reset, Load_i, Exec, PushLoad, PopLoad, r_w, start_mc, fetch, Stop

  assign Kbd_Clear = Reset;

  // Other names for the same wires on the sheet: CLK = Clock; CS = Chip_Select; KBD_AVAIL = Kbd_Available;
  //   CLR = Reset; KBD_CLR = Reset; KBD_DATA[6:0] = Kbd_ASCII_Data; RAM_A[15:0] = Address;
  //   RAM_INPUT_0[31:0] = RAM_In_0; RAM_INPUT_1[31:0] = RAM_In_1; RAM_INPUT_2[31:0] = RAM_In_2;
  //   RAM_INPUT_3[31:0] = RAM_In_3; RAM_MASK[3:0] = Mask; RAM_OUTPUT_0[31:0] = RAM_Out_0;
  //   RAM_OUTPUT_1[31:0] = RAM_Out_1; RAM_OUTPUT_2[31:0] = RAM_Out_2; RAM_OUTPUT_3[31:0] = RAM_Out_3;
  //   RW = nRead_Write; TTY_DATA[6:0] = TTY_ASCII_Data

  // Notes on the sheet:
  //   RAM ADDRESS
  //   DATA FROM RAM
  //   DATA TO RAM
  //   DATA WRITE MASK
  //   RAM TIMING
  //   RAM CONTROL
  //   KEYBOARD
  //   TTY
  //   SEQUENCING
endmodule

module RAM_2 (
  input  [15:0] Address,
  input  [31:0] Data_In_0,
  input  [31:0] Data_In_1,
  input  [31:0] Data_In_2,
  input  [31:0] Data_In_3,
  input  [3:0] Mask,
  input  nRead_Write,
  input  Chip_Select,
  input  Reset,
  output [31:0] Data_Out_0,
  output [31:0] Data_Out_1,
  output [31:0] Data_Out_2,
  output [31:0] Data_Out_3,
  output [3:0] Read_Time,
  output [3:0] Write_Time
);

  wire and_2_out, and_3_out, and_4_out, and_5_out, and_6_out, and_7_out, and_8_out, and_9_out, Changed, CLK,
       comparator_2_eq, comparator_3_eq, comparator_4_eq, comparator_5_eq, comparator_6_eq, Count,
       demultiplexer_3_out0, Idle, Idle_q, Load, Load0, Load1, nand_1_out, or_1_out, or_2_out, or_3_out,
       or_4_out, or_5_out, or_6_out, or_7_out, or_8_out, or_9_out, or_10_out, Proc_q, Update_Mem, Zero_Time;
  wire [3:0] counter_1_q, multiplexer_1_out, subtractor_1_out;
  wire [31:0] register_1_q, register_2_q, register_3_q, register_4_q, register_5_q;

  // Probe on 4'b0011
  // Probe on 4'b0010
  Multiplexer #(.width(4), .enable("false")) multiplexer_1 (
    .in0(4'b0011), .in1(4'b0010), .out(multiplexer_1_out), .sel(nRead_Write));
  or or_1 (or_1_out, Idle, Update_Mem);
  or or_2 (or_2_out, ~Chip_Select, Reset);  // OR_Gate
  Subtractor #(.width(4)) subtractor_1 (.a(multiplexer_1_out), .b(4'b0010), .out(subtractor_1_out));  // open: bin, bout
  Demultiplexer #(.enable("false")) demultiplexer_1 (.out0(Idle), .out1(Load0), .in(Idle_q), .sel(Changed));
  D_Flip_Flop u_Idle (.clk(CLK), .D(or_1_out), .Q(Idle_q), .preset(or_2_out));  // open: Qn, en, reset
  // Probe on counter_1_q
  Counter #(.width(4), .max('hf)) counter_1 (
    .load(Load), .D(subtractor_1_out), .count(Count), .Q(counter_1_q), .clk(CLK), .clr(or_3_out));  // open: carry
  or or_3 (or_3_out, ~Chip_Select, Reset);  // OR_Gate
  Comparator #(.width(4), .mode("unsigned")) comparator_1 (
    .a(4'b0000), .b(counter_1_q), .eq(Zero_Time));  // open: gt, lt
  or or_4 (or_4_out, Count, Load0, Load1);
  Register #(.width(32)) register_1 (.D(Data_In_0), .en(Chip_Select), .Q(register_1_q), .clk(CLK), .clr(or_5_out));
  or or_5 (or_5_out, ~Chip_Select, Reset);  // OR_Gate
  Register #(.width(32)) register_2 (.D(Data_In_1), .en(Chip_Select), .Q(register_2_q), .clk(CLK), .clr(or_6_out));
  or or_6 (or_6_out, ~Chip_Select, Reset);  // OR_Gate
  Register #(.width(32)) register_3 (.D(Data_In_2), .en(Chip_Select), .Q(register_3_q), .clk(CLK), .clr(or_7_out));
  or or_7 (or_7_out, ~Chip_Select, Reset);  // OR_Gate
  Register #(.width(32)) register_4 (.D(Data_In_3), .en(Chip_Select), .Q(register_4_q), .clk(CLK), .clr(or_8_out));
  or or_8 (or_8_out, ~Chip_Select, Reset);  // OR_Gate
  Register #(.width(32)) register_5 (
    .D({{11{1'b1}}, nRead_Write, Mask, Address}), .en(Chip_Select), .Q(register_5_q), .clk(CLK),
    .clr(or_9_out));
  or or_9 (or_9_out, ~Chip_Select, Reset);  // OR_Gate
  D_Flip_Flop Proc (.clk(CLK), .D(or_4_out), .Q(Proc_q), .reset(or_10_out));  // open: Qn, preset, en
  or or_10 (or_10_out, ~Chip_Select, Reset);  // OR_Gate
  Demultiplexer #(.enable("false")) demultiplexer_2 (
    .out0(Count), .out1(Update_Mem), .in(demultiplexer_3_out0), .sel(Zero_Time));
  Demultiplexer #(.enable("false")) demultiplexer_3 (
    .out0(demultiplexer_3_out0), .out1(Load1), .in(Proc_q), .sel(Changed));
  Clock clock_1 (.out(CLK));
  Comparator #(.width(32)) comparator_2 (.a(register_1_q), .b(Data_In_0), .eq(comparator_2_eq));  // open: gt, lt
  Comparator #(.width(32)) comparator_3 (.a(register_2_q), .b(Data_In_1), .eq(comparator_3_eq));  // open: gt, lt
  Comparator #(.width(32)) comparator_4 (.a(register_3_q), .b(Data_In_2), .eq(comparator_4_eq));  // open: gt, lt
  Comparator #(.width(32)) comparator_5 (.a(register_4_q), .b(Data_In_3), .eq(comparator_5_eq));  // open: gt, lt
  Comparator #(.width(32)) comparator_6 (
    .a(register_5_q), .b({{11{1'b1}}, nRead_Write, Mask, Address}), .eq(comparator_6_eq));  // open: gt, lt
  nand nand_1 (nand_1_out, comparator_6_eq, comparator_2_eq, comparator_3_eq, comparator_4_eq, comparator_5_eq);
  and and_1 (Changed, nand_1_out, Chip_Select);
  or or_11 (Load, Count, Load1, Load0);
  and and_2 (and_2_out, Mask[0], Update_Mem, nRead_Write);
  and and_3 (and_3_out, Mask[1], Update_Mem, nRead_Write);
  and and_4 (and_4_out, Mask[2], Update_Mem, nRead_Write);
  and and_5 (and_5_out, Mask[3], Update_Mem, nRead_Write);
  RAM_part #(.addrWidth(16), .dataWidth(32), .bus("separate")) ram_1 (
    .addr(Address), .din(Data_In_0), .data(Data_Out_0), .str(and_2_out), .sel(Chip_Select), .clk(CLK),
    .ld(and_6_out), .clr(Reset));
  and and_6 (and_6_out, ~nRead_Write, Idle);  // AND_Gate
  RAM_part #(.addrWidth(16), .dataWidth(32), .bus("separate")) ram_2 (
    .addr(Address), .din(Data_In_1), .data(Data_Out_1), .str(and_3_out), .sel(Chip_Select), .clk(CLK),
    .ld(and_7_out), .clr(Reset));
  and and_7 (and_7_out, ~nRead_Write, Idle);  // AND_Gate
  RAM_part #(.addrWidth(16), .dataWidth(32), .bus("separate")) ram_3 (
    .addr(Address), .din(Data_In_2), .data(Data_Out_2), .str(and_4_out), .sel(Chip_Select), .clk(CLK),
    .ld(and_8_out), .clr(Reset));
  and and_8 (and_8_out, ~nRead_Write, Idle);  // AND_Gate
  RAM_part #(.addrWidth(16), .dataWidth(32), .bus("separate")) ram_4 (
    .addr(Address), .din(Data_In_3), .data(Data_Out_3), .str(and_5_out), .sel(Chip_Select), .clk(CLK),
    .ld(and_9_out), .clr(Reset));
  and and_9 (and_9_out, ~nRead_Write, Idle);  // AND_Gate

  assign Read_Time = 4'b0011;
  assign Write_Time = 4'b0010;

  // Other names for the same wires on the sheet: M0 = Mask[0]; M1 = Mask[1]; M2 = Mask[2]; M3 = Mask[3];
  //   RW = nRead_Write; CLR = Reset; CS = Chip_Select; Load2 = Count

  // Notes on the sheet:
  //   NO MODIFICAR
  //   excepto quizás los valores RT y WT
  //   BANK0
  //   BANK1
  //   BANK2
  //   BANK3
endmodule

module RAM_Dispatcher (
  input  [3:0] WriteTime,
  input  Clock,
  input  CLR,
  output [31:0] Data,
  output [15:0] Address,
  output [3:0] Mask,
  output Finished,
  output Write
);

  wire demultiplexer_2_out1, demultiplexer_3_out1, End, IDLE_q, IncAddr, Load, or_1_out, or_2_out, While_q,
       WriteEnd;
  wire [3:0] counter_1_q;
  wire [31:0] CurrentAddress_q;

  Counter #(.width(32), .max('hffffffff)) CurrentAddress (
    .count(IncAddr), .Q({CurrentAddress_q[31:18], Address, CurrentAddress_q[1:0]}), .clk(Clock), .clr(CLR));  // open: load, D, carry
  or or_1 (or_1_out, IncAddr, demultiplexer_3_out1, Finished);
  D_Flip_Flop IDLE (.clk(Clock), .D(or_1_out), .Q(IDLE_q), .preset(CLR));  // open: Qn, en, reset
  Demultiplexer #(.enable("false")) demultiplexer_1 (.out0(Load), .out1(Finished), .in(IDLE_q), .sel(End));
  D_Flip_Flop While (.clk(Clock), .D(or_2_out), .Q(While_q), .reset(CLR));  // open: Qn, preset, en
  or or_2 (or_2_out, Write, Load);
  RAM_part #(.addrWidth(18), .dataWidth(32)) ram_1 (
    .addr({Address, CurrentAddress_q[1:0]}), .data(Data), .clk(Clock));  // open: sel, ld, clr
  Demultiplexer #(.enable("false")) demultiplexer_2 (
    .out0(Write), .out1(demultiplexer_2_out1), .in(While_q), .sel(WriteEnd));
  Decoder #(.select(2)) decoder_1 (
    .out0(Mask[0]), .out1(Mask[1]), .out2(Mask[2]), .out3(Mask[3]), .sel(CurrentAddress_q[1:0]));  // open: en
  Demultiplexer #(.enable("false")) demultiplexer_3 (
    .out0(IncAddr), .out1(demultiplexer_3_out1), .in(demultiplexer_2_out1), .sel(End));
  Counter #(.width(4), .max('hf)) counter_1 (
    .load(Load), .D(WriteTime), .count(Write), .Q(counter_1_q), .clk(Clock));  // open: carry, clr
  Comparator #(.width(32)) comparator_1 (.a(Data), .b({32{1'b1}}), .eq(End));  // open: gt, lt
  Comparator #(.width(4)) comparator_2 (.a(4'b0000), .b(counter_1_q), .eq(WriteEnd));  // open: gt, lt

  // Other names for the same wires on the sheet: CLK = Clock; Count = Write; WT[3:0] = WriteTime
endmodule

module CONTROL_UNIT (
  input  Start,
  input  Clock,
  input  RST,
  input  [5:0] Op_code,
  input  [5:0] Func_code,
  input  Ready_Inst,
  input  Ready_Data,
  input  Ready_Write,
  output Read_Instruction,
  output Load_Instruction,
  output Read_Data,
  output Write_Data,
  output Register_Enable,
  output Pogram_Counter_Enable,
  output Stack_Pointer_Enable,
  output KBD_Enable,
  output Type_I,
  output MFHI,
  output MFLO,
  output Pop_En,
  output Push_En,
  output Lw_En,
  output Sw_En,
  output KBD,
  output RND,
  output TTY,
  output End
);

  wire ALU, and_1_out, and_2_out, and_3_out, comparator_1_eq, comparator_2_eq, comparator_3_eq,
       comparator_4_eq, comparator_5_eq, comparator_6_eq, comparator_9_eq, comparator_10_eq,
       comparator_11_eq, comparator_12_eq, comparator_13_eq, Cpy, demultiplexer_1_out0, demultiplexer_1_out1,
       demultiplexer_2_out0, demultiplexer_3_out0, demultiplexer_4_out0, Halt, I, IDLE_q, J, Jmp, KBD_t, Lw,
       MFHI_t, MFLO_t, Mry, or_1_out, or_2_out, or_3_out, or_6_out, or_7_out, Pop, Push, R, RND_t, SP1, SP2,
       Spc, Start_Enables, Sw, Tty_t, TtyEn, Wait_3_q, Wait_4_q, Wait_5_q, Wait_8_q, Wait_q;

  and and_1 (and_1_out, Spc, RND_t);
  and and_2 (and_2_out, Spc, KBD_t);
  and and_3 (and_3_out, Spc, Halt);
  Demultiplexer #(.enable("false")) demultiplexer_1 (
    .out0(demultiplexer_1_out0), .out1(demultiplexer_1_out1), .in(IDLE_q), .sel(Start));
  D_Flip_Flop #(.trigger("falling")) IDLE (
    .clk(Clock), .D(demultiplexer_1_out0), .Q(IDLE_q), .preset(RST));  // open: Qn, en, reset
  or or_1 (or_1_out, ALU, Cpy, Ready_Data, and_1_out, and_2_out);
  D_Flip_Flop #(.trigger("falling")) Wait (.clk(Clock), .D(Mry), .Q(Wait_q), .reset(RST));  // open: Qn, preset, en
  Demultiplexer #(.enable("false")) demultiplexer_2 (
    .out0(demultiplexer_2_out0), .out1(Read_Data), .in(Wait_q), .sel(or_3_out));
  or or_2 (or_2_out, End, and_3_out);
  D_Flip_Flop #(.trigger("falling")) Wait_2 (
    .clk(Clock), .D(or_1_out), .Q(Register_Enable), .reset(RST));  // open: Qn, preset, en
  or or_3 (or_3_out, Lw, Pop);
  D_Flip_Flop #(.trigger("falling")) u_End (.clk(Clock), .D(or_2_out), .Q(End), .reset(RST));  // open: Qn, preset, en
  or or_4 (Read_Instruction, demultiplexer_1_out1, Pogram_Counter_Enable);
  Demultiplexer #(.enable("false")) demultiplexer_3 (
    .out0(demultiplexer_3_out0), .out1(SP2), .in(demultiplexer_2_out0), .sel(Push));
  D_Flip_Flop #(.trigger("falling")) Wait_3 (
    .clk(Clock), .D(Register_Enable), .Q(Wait_3_q), .reset(RST));  // open: Qn, preset, en
  Demultiplexer #(.enable("false")) demultiplexer_4 (.out0(demultiplexer_4_out0), .out1(SP1), .in(Wait_3_q), .sel(Pop));
  and and_4 (TtyEn, Spc, Tty_t);
  and and_5 (KBD_Enable, KBD_t, demultiplexer_4_out0);
  or or_5 (Write_Data, demultiplexer_3_out0, Wait_4_q);
  D_Flip_Flop #(.trigger("falling")) Wait_4 (.clk(Clock), .D(SP2), .Q(Wait_4_q), .reset(RST));  // open: Qn, preset, en
  or or_6 (or_6_out, demultiplexer_4_out0, Wait_5_q);
  D_Flip_Flop #(.trigger("falling")) Wait_5 (.clk(Clock), .D(SP1), .Q(Wait_5_q), .reset(RST));  // open: Qn, preset, en
  D_Flip_Flop #(.trigger("falling")) Wait_6 (
    .clk(Clock), .D(Ready_Inst), .Q(Start_Enables), .reset(RST));  // open: Qn, preset, en
  D_Flip_Flop #(.trigger("falling")) Wait_7 (
    .clk(Clock), .D(or_7_out), .Q(Pogram_Counter_Enable), .reset(RST));  // open: Qn, preset, en
  or or_7 (or_7_out, or_6_out, Jmp, Ready_Write, TtyEn);
  Operation_Decoder operation_decoder_1 (
    .Op_code(Op_code), .Func_code(Func_code), .Type_R(R), .Type_I(I), .Type_J(J), .Copy_Inst(Cpy),
    .Jump_Inst(Jmp), .Memory_Inst(Mry), .Special_Inst(Spc), .ALU_Inst(ALU), .Enable(Start_Enables));
  Comparator #(.width(6)) comparator_1 (.a(Op_code), .b({6{1'b0}}), .eq(comparator_1_eq));  // open: gt, lt
  Comparator #(.width(6)) comparator_2 (.a(Func_code), .b(6'b010010), .eq(comparator_2_eq));  // open: gt, lt
  and and_6 (MFLO_t, comparator_2_eq, comparator_1_eq);
  and and_7 (MFHI_t, comparator_1_eq, comparator_3_eq);
  Comparator #(.width(6)) comparator_3 (.a(Func_code), .b(6'b010000), .eq(comparator_3_eq));  // open: gt, lt
  Comparator #(.width(6)) comparator_4 (.a(Op_code), .b(6'b111000), .eq(comparator_4_eq));  // open: gt, lt
  and and_8 (Pop, comparator_4_eq, comparator_5_eq);
  Comparator #(.width(6)) comparator_5 (.a(Func_code), .b({6{1'b0}}), .eq(comparator_5_eq));  // open: gt, lt
  and and_9 (Push, comparator_4_eq, comparator_6_eq);
  Comparator #(.width(6)) comparator_6 (.a(Func_code), .b(6'b000001), .eq(comparator_6_eq));  // open: gt, lt
  Comparator #(.width(6)) comparator_7 (.a(Op_code), .b(6'b100011), .eq(Lw));  // open: gt, lt
  Comparator #(.width(6)) comparator_8 (.a(Op_code), .b(6'b101011), .eq(Sw));  // open: gt, lt
  Comparator #(.width(6)) comparator_9 (.a(Op_code), .b({6{1'b1}}), .eq(comparator_9_eq));  // open: gt, lt
  and and_10 (RND_t, comparator_9_eq, comparator_10_eq);
  Comparator #(.width(6)) comparator_10 (.a(Func_code), .b(6'b000010), .eq(comparator_10_eq));  // open: gt, lt
  and and_11 (KBD_t, comparator_9_eq, comparator_11_eq);
  Comparator #(.width(6)) comparator_11 (.a(Func_code), .b(6'b000100), .eq(comparator_11_eq));  // open: gt, lt
  and and_12 (Tty_t, comparator_9_eq, comparator_12_eq);
  Comparator #(.width(6)) comparator_12 (.a(Func_code), .b(6'b000001), .eq(comparator_12_eq));  // open: gt, lt
  and and_13 (Halt, comparator_9_eq, comparator_13_eq);
  Comparator #(.width(6)) comparator_13 (.a(Func_code), .b({6{1'b1}}), .eq(comparator_13_eq));  // open: gt, lt
  or or_8 (Stack_Pointer_Enable, SP2, SP1);
  and and_14 (Type_I, I, Wait_8_q);
  and and_15 (MFHI, MFHI_t, Wait_8_q);
  and and_16 (MFLO, MFLO_t, Wait_8_q);
  and and_17 (Pop_En, Pop, Wait_8_q);
  and and_18 (Push_En, Push, Wait_8_q);
  and and_19 (Lw_En, Lw, Wait_8_q);
  and and_20 (Sw_En, Sw, Wait_8_q);
  and and_21 (KBD, KBD_t, Wait_8_q);
  and and_22 (RND, RND_t, Wait_8_q);
  and and_23 (TTY, TtyEn, Wait_8_q);
  D_Flip_Flop #(.trigger("falling")) Wait_8 (
    .clk(Clock), .Q(Wait_8_q), .preset(Start_Enables), .reset(Pogram_Counter_Enable));  // open: D, Qn, en

  assign Load_Instruction = Ready_Inst;

  // Other names for the same wires on the sheet: CLK = Clock; CLR = RST; Load_Inst = Ready_Inst;
  //   Read_Inst = Read_Instruction; RegEN = Register_Enable; SPEN = Stack_Pointer_Enable;
  //   PCEN = Pogram_Counter_Enable; Stop_Enables = Pogram_Counter_Enable

  // Notes on the sheet:
  //   Flags
endmodule

module Operation_Decoder (
  input  [5:0] Op_code,
  input  [5:0] Func_code,
  input  Enable,
  output Type_R,
  output Type_I,
  output Type_J,
  output Copy_Inst,
  output Jump_Inst,
  output Memory_Inst,
  output Special_Inst,
  output ALU_Inst
);

  wire _000000, _111000, _111111, and_3_out, and_4_out, and_5_out, and_6_out, and_7_out, comparator_1_eq,
       comparator_5_eq, comparator_6_eq, comparator_7_eq, comparator_8_eq, comparator_9_lt, comparator_10_eq,
       comparator_11_eq, nor_1_out, not_1_out, not_2_out, or_2_out, or_3_out, or_4_out;

  not not_1 (not_1_out, Type_R);
  not not_2 (not_2_out, comparator_1_eq);
  Comparator #(.width(6)) comparator_1 (.a(Op_code), .b(6'b000010), .eq(comparator_1_eq));  // open: gt, lt
  or or_1 (Type_R, _000000, _111000, _111111);
  and and_1 (Type_I, not_2_out, not_1_out);
  and and_2 (Type_J, comparator_1_eq, not_1_out);
  Comparator #(.width(6)) comparator_2 (.a(Op_code), .b({6{1'b0}}), .eq(_000000));  // open: gt, lt
  Comparator #(.width(6)) comparator_3 (.a(Op_code), .b(6'b111000), .eq(_111000));  // open: gt, lt
  Comparator #(.width(6)) comparator_4 (.a(Op_code), .b({6{1'b1}}), .eq(_111111));  // open: gt, lt
  Comparator #(.width(6)) comparator_5 (.a(Func_code), .b(6'b010010), .eq(comparator_5_eq));  // open: gt, lt
  and and_3 (and_3_out, comparator_5_eq, _000000);
  and and_4 (and_4_out, _000000, comparator_6_eq);
  Comparator #(.width(6)) comparator_6 (.a(Func_code), .b(6'b010000), .eq(comparator_6_eq));  // open: gt, lt
  Comparator #(.width(6)) comparator_7 (.a(Func_code), .b({6{1'b0}}), .eq(comparator_7_eq));  // open: gt, lt
  and and_5 (and_5_out, comparator_7_eq, _000000);
  and and_6 (and_6_out, _000000, comparator_8_eq);
  Comparator #(.width(6)) comparator_8 (.a(Func_code), .b(6'b001000), .eq(comparator_8_eq));  // open: gt, lt
  Comparator #(.width(6), .mode("unsigned")) comparator_9 (
    .a(Op_code), .b(6'b001000), .lt(comparator_9_lt));  // open: gt, eq
  and and_7 (and_7_out, comparator_9_lt, Type_I);
  Comparator #(.width(6)) comparator_10 (.a(Op_code), .b(6'b100011), .eq(comparator_10_eq));  // open: gt, lt
  Comparator #(.width(6)) comparator_11 (.a(Op_code), .b(6'b101011), .eq(comparator_11_eq));  // open: gt, lt
  or or_2 (or_2_out, and_3_out, and_4_out);
  or or_3 (or_3_out, and_5_out, and_6_out, and_7_out);
  or or_4 (or_4_out, _111000, comparator_10_eq, comparator_11_eq);
  nor nor_1 (nor_1_out, Copy_Inst, Jump_Inst, Memory_Inst, Special_Inst);
  and and_8 (Copy_Inst, Enable, or_2_out);
  and and_9 (Jump_Inst, Enable, or_3_out);
  and and_10 (Memory_Inst, Enable, or_4_out);
  and and_11 (Special_Inst, Enable, _111111);
  and and_12 (ALU_Inst, Enable, nor_1_out);

  // Other names for the same wires on the sheet: EN = Enable
endmodule

module DATA_PATH (
  input  Clock,
  input  Reset,
  input  Load_I,
  input  Execute_i,
  input  [31:0] Instruction_in,
  input  [31:0] Data_in,
  input  [6:0] KBD_data,
  input  KBD_avail,
  input  PushLoad,
  input  PopLoad,
  output Push,
  output [31:0] PC_out,
  output Pop,
  output KBD_Enable,
  output [31:0] mem_address,
  output [31:0] mem_write_data,
  output Halt,
  output Memory_neede,
  output is_write,
  output [6:0] TTY_data,
  output TTY_enable
);

  wire ADDI, and_1_out, and_2_out, ANDI, BEQ, BGTZ, BLEZ, BLTZ, BNE, IS_ALU, IS_MULT, J, JR, LW, MFHI, MFLO,
       nop, or_4_out, or_5_out, ORI, r_w, RND, SIGN, SLTI, SLTIU, SW, USE_IMM, USE_RT, WR_EN, WR_HL, XORI,
       ZERO;
  wire [2:0] WR_SEL;
  wire [3:0] ALU_OP;
  wire [4:0] RD, RS, RT, WR_REG;
  wire [15:0] IMM;
  wire [25:0] JUMP_ADDR;
  wire [31:0] adder_2_out, ALU_B, bit_extender_1_out, HI_IN, HI_OUT, IMM_EXT, INSTRUCTION, KBD_EXT, LO_IN,
       LO_OUT, multiplexer_5_out, NEXT_PC, PC_PLUS4, RND_DATA, SP, SP_Mod, subtractor_1_out, WR_DATA;
  wire [31:7] RS_DATA;

  and and_1 (and_1_out, Pop, PopLoad);
  assign bit_extender_1_out = {{25{1'b0}}, KBD_data};  // Bit_Extender bit_extender_1
  or or_1 (USE_IMM, SLTIU, ADDI, ANDI, ORI, XORI, LW, SW, SLTI);
  or or_2 (WR_EN, IS_ALU, USE_RT, KBD_Enable, RND, and_1_out);
  Multiplexer #(.width(32), .enable("false")) multiplexer_1 (
    .in0({32{1'b1}}), .in1(bit_extender_1_out), .out(KBD_EXT), .sel(KBD_avail));
  or or_3 (is_write, SW, Push);
  Instruction_Register instruction_register_1 (
    .Instruction(Instruction_in), .Enable(Load_I), .Instruction_2(INSTRUCTION), .Clk(Clock), .RST(Reset));
  Instruction_Decoder instruction_decoder_1 (
    .Instruction(INSTRUCTION), .Constant(IMM), .Destine(JUMP_ADDR), .RS(RS), .RT(RT), .RD(RD),
    .ALU_Selector(ALU_OP), .ADDI(ADDI), .ANDI(ANDI), .ORI(ORI), .XORI(XORI), .BLTZ(BLTZ), .BEQ(BEQ),
    .BNE(BNE), .BLEZ(BLEZ), .BGTZ(BGTZ), .SLTI(SLTI), .SLTIU(SLTIU), .LW(LW), .SW(SW), .WrHL(WR_HL),
    .Wr(r_w), .IsALU(IS_ALU), .Jump(J), .push(Push), .pop(Pop), .mfhi(MFHI), .mflo(MFLO), .jr(JR), .nop(nop),
    .tty(TTY_enable), .rnd(RND), .kbd(KBD_Enable), .halt(Halt));
  or or_4 (or_4_out, LW, Pop);
  or or_5 (or_5_out, Push, and_2_out);
  and and_2 (and_2_out, Pop, PopLoad);
  or or_6 (USE_RT, SLTIU, ADDI, ANDI, ORI, XORI, LW, SLTI);
  Multiplexer #(.width(5), .enable("false")) multiplexer_2 (.in0(RD), .in1(RT), .out(WR_REG), .sel(USE_RT));
  Priority_Encoder priority_encoder_1 (
    .in0(1'b1), .in1(or_4_out), .in2(MFHI), .in3(MFLO), .in4(KBD_Enable), .in5(RND), .in6(or_5_out),
    .out(WR_SEL));  // open: in7, en_in, gs, en_out
  Register_File register_file_1 (
    .DataIncome(WR_DATA), .DataAddress(WR_REG), .Selector_A(RS), .Selector_B(RT), .Hi_in(HI_IN),
    .Lo_in(LO_IN), .Reset(Reset), .Clock(Clock), .in_9(WR_HL), .WriteEnable(WR_EN),
    .OutA({RS_DATA, TTY_data}), .OutB(mem_write_data), .Hi_out(HI_OUT), .Lo_out(LO_OUT), .SP(SP));
  Multiplexer #(.select(3), .width(32), .enable("false")) multiplexer_3 (
    .in0(mem_address), .in1(Data_in), .in2(HI_OUT), .in3(LO_OUT), .in4(KBD_EXT), .in5(RND_DATA),
    .in6(SP_Mod), .in7(PC_PLUS4), .out(WR_DATA), .sel(WR_SEL));
  or or_7 (Memory_neede, LW, SW, Push, Pop);
  Random #(.width(32)) random_1 (.clk(Clock), .next(RND), .out(RND_DATA));  // open: clr
  Adder #(.width(32)) adder_1 (.a(PC_out), .b(32'h4), .out(PC_PLUS4));  // open: cin, cout
  ALU alu_1 (
    .A({RS_DATA, TTY_data}), .B(ALU_B), .Select(ALU_OP), .Out(mem_address), .Hi(HI_IN), .Lo(LO_IN),
    .Sign(SIGN), .IsMult(IS_MULT), .Zero(ZERO));
  assign IMM_EXT = {{16{IMM[15]}}, IMM};  // Bit_Extender bit_extender_2
  Multiplexer #(.width(32), .enable("false")) multiplexer_4 (
    .in0(mem_write_data), .in1(IMM_EXT), .out(ALU_B), .sel(USE_IMM));
  Adder #(.width(32)) adder_2 (.a(SP), .b(32'h4), .out(adder_2_out));  // open: cin, cout
  Subtractor #(.width(32)) subtractor_1 (.a(SP), .b(32'h4), .out(subtractor_1_out));  // open: bin, bout
  Multiplexer #(.width(32), .enable("false")) multiplexer_5 (
    .in0(SP), .in1(adder_2_out), .out(multiplexer_5_out), .sel(Pop));
  Program_Counter program_counter_1 (
    .PC_New(NEXT_PC), .Enable(Execute_i), .Clk(Clock), .RST(Reset), .PC_Actual(PC_out));
  Branch_Control branch_control_1 (
    .PC(PC_out), .offset(IMM), .Address(JUMP_ADDR), .Register_Value({RS_DATA, TTY_data}), .Zero(ZERO),
    .Sng(SIGN), .BLEZ(BLEZ), .BGTZ(BGTZ), .BLTZ(BLTZ), .BEQ(BEQ), .BNE(BNE), .J(J), .Jr(JR), .Next_PC(NEXT_PC));
  Multiplexer #(.width(32), .enable("false")) multiplexer_6 (
    .in0(multiplexer_5_out), .in1(subtractor_1_out), .out(SP_Mod), .sel(Push));

  // Other names for the same wires on the sheet: ALU_OUT[31:0] = mem_address; CLK = Clock; EXECUTE = Execute_i;
  //   INST_IN[31:0] = Instruction_in; KBD = KBD_Enable; MEM_NEED = Memory_neede; PC[31:0] = PC_out;
  //   RS_DATA[6:0] = TTY_data; TTY_DATA_OUT[6:0] = TTY_data; RST = Reset; RT_DATA[31:0] = mem_write_data;
  //   TTY = TTY_enable

  // Notes on the sheet:
  //   Input
  //   Instruction Fetch
  //   Output
  //   Register File
  //   Arithmetic Control Unit
  //   Branch Control
endmodule

module Branch_Control (
  input  [31:0] PC,
  input  [15:0] offset,
  input  [25:0] Address,
  input  [31:0] Register_Value,
  input  Zero,
  input  Sng,
  input  BLEZ,
  input  BGTZ,
  input  BLTZ,
  input  BEQ,
  input  BNE,
  input  J,
  input  Jr,
  output [31:0] Next_PC
);

  wire and_1_out, and_2_out, and_3_out, and_4_out, and_5_out, and_6_out, or_1_out, sel;
  wire [31:0] multiplexer_1_out, multiplexer_2_out, PC_4, PC_4_4_offset;
  wire [31:18] sng_extend_offset_____2;

  or or_1 (or_1_out, Sng, Zero);
  and and_1 (and_1_out, BEQ, Zero);
  and and_2 (and_2_out, BLEZ, or_1_out);
  Multiplexer #(.width(32), .enable("false")) multiplexer_1 (
    .in0(PC_4), .in1(PC_4_4_offset), .out(multiplexer_1_out), .sel(sel));
  and and_3 (and_3_out, BNE, ~Zero);  // AND_Gate
  and and_4 (and_4_out, BGTZ, and_5_out);
  and and_5 (and_5_out, ~Sng, ~Zero);  // AND_Gate
  Multiplexer #(.width(32), .enable("false")) multiplexer_2 (
    .in0(multiplexer_1_out), .in1(Register_Value), .out(multiplexer_2_out), .sel(Jr));
  and and_6 (and_6_out, BLTZ, Sng);
  Multiplexer #(.width(32), .enable("false")) multiplexer_3 (
    .in0(multiplexer_2_out), .in1({PC[31:28], Address, 2'b00}), .out(Next_PC), .sel(J));
  or or_2 (sel, and_1_out, and_3_out, and_2_out, and_4_out, and_6_out);
  Adder #(.width(32)) adder_1 (.a(PC), .b(32'h4), .out(PC_4));  // open: cin, cout
  assign sng_extend_offset_____2 = {{13{offset[15]}}, offset[15]};  // Bit_Extender bit_extender_1
  Adder #(.width(32)) adder_2 (
    .a(PC_4), .b({sng_extend_offset_____2, offset, 2'b00}), .out(PC_4_4_offset));  // open: cin, cout

  // Other names for the same wires on the sheet: Destine[31:2] = {PC[31:28], Address}; Next[31:0] = Next_PC;
  //   RV[31:0] = Register_Value; sng_extend_offset_____2[17:2] = offset; Z = Zero

  // Notes on the sheet:
  //   Input
  //   Sub Case Selection 
  //   Output
  //   Calculate operation
endmodule

module Program_Counter (
  input  [31:0] PC_New,
  input  Enable,
  input  Clk,
  input  RST,
  output [31:0] PC_Actual
);

  Register #(.width(32)) register_1 (.D(PC_New), .en(Enable), .Q(PC_Actual), .clk(Clk), .clr(RST));
endmodule

module ALU (
  input  [31:0] A,
  input  [31:0] B,
  input  [3:0] Select,
  output [31:0] Out,
  output [31:0] Hi,
  output [31:0] Lo,
  output Sign,
  output Zero,
  output IsMult
);

  wire comparator_1_lt, comparator_2_lt, not_1_out, not_2_out, not_3_out;
  wire [31:0] ADD, AND, and_2_out, Div_Hi, Div_Hi_u, Div_Lo, Div_Lo_u, Mult_Hi, Mult_Hi_u, Mult_Lo,
       Mult_Lo_u, multiplexer_1_out, multiplexer_3_out, multiplexer_5_out, multiplexer_7_out,
       multiplexer_10_out, NOR, OR, SLT, SLT_u, SUB, XOR;

  Multiplexer #(.select(3), .width(32)) multiplexer_1 (
    .in0(ADD), .in1(SUB), .in2(AND), .in3(OR), .in4(NOR), .in5(XOR), .in6(SLT), .in7(SLT_u),
    .out(multiplexer_1_out), .sel(Select[2:0]), .en(not_1_out));
  not not_1 (not_1_out, Select[3]);
  Multiplexer #(.width(32), .enable("false")) multiplexer_2 (
    .in0(multiplexer_1_out), .in1({32{1'b0}}), .out(Out), .sel(Select[3]));
  Adder #(.width(32)) adder_1 (.a(A), .b(B), .out(ADD));  // open: cin, cout
  Subtractor #(.width(32)) subtractor_1 (.a(A), .b(B), .out(SUB));  // open: bin, bout
  Multiplier #(.width(32)) multiplier_1 (.a(A), .b(B), .out(Mult_Lo), .cout(Mult_Hi));  // open: cin
  Divider #(.width(32)) divider_1 (.a(A), .b(B), .out(Div_Lo), .rem(Div_Hi));  // open: upper
  Multiplexer #(.select(2), .width(32)) multiplexer_3 (
    .in0(Mult_Hi), .in1(Mult_Hi_u), .in2(Div_Hi), .in3(Div_Hi_u), .out(multiplexer_3_out), .sel(Select[1:0]),
    .en(Select[3]));
  MULU mulu_1 (.A(A), .B(B), .Lo(Mult_Lo_u), .Hi(Mult_Hi_u));
  DIVU divu_1 (.A(A), .B(B), .Result(Div_Lo_u), .Remainder(Div_Hi_u));
  Multiplexer #(.width(32), .enable("false")) multiplexer_4 (
    .in0(multiplexer_3_out), .in1({32{1'b0}}), .out(Hi), .sel(not_2_out));
  not not_2 (not_2_out, Select[3]);
  Multiplexer #(.select(2), .width(32)) multiplexer_5 (
    .in0(Mult_Lo), .in1(Mult_Lo_u), .in2(Div_Lo), .in3(Div_Lo_u), .out(multiplexer_5_out), .sel(Select[1:0]),
    .en(Select[3]));
  assign AND = A & B;  // AND_Gate and_1, 32 bits wide
  assign OR = A | B;  // OR_Gate or_1, 32 bits wide
  assign NOR = ~(A | B);  // NOR_Gate nor_1, 32 bits wide
  assign XOR = A ^ B;  // XOR_Gate xor_1, 32 bits wide
  Multiplexer #(.width(32), .enable("false")) multiplexer_6 (
    .in0(multiplexer_5_out), .in1({32{1'b0}}), .out(Lo), .sel(not_3_out));
  not not_3 (not_3_out, Select[3]);
  Comparator #(.width(32)) comparator_1 (.a(A), .b(B), .lt(comparator_1_lt));  // open: gt, eq
  Comparator #(.width(32), .mode("unsigned")) comparator_2 (.a(A), .b(B), .lt(comparator_2_lt));  // open: gt, eq
  Multiplexer #(.width(32), .enable("false")) multiplexer_7 (
    .in0(Out), .in1(Hi), .out(multiplexer_7_out), .sel(Select[3]));
  assign and_2_out = Hi & Lo;  // AND_Gate and_2, 32 bits wide
  Multiplexer #(.width(32), .enable("false")) multiplexer_8 (
    .in0({32{1'b0}}), .in1(32'h1), .out(SLT), .sel(comparator_1_lt));
  Multiplexer #(.width(32), .enable("false")) multiplexer_9 (
    .in0({32{1'b0}}), .in1(32'h1), .out(SLT_u), .sel(comparator_2_lt));
  Comparator #(.width(32)) comparator_3 (.a(multiplexer_7_out), .b({32{1'b0}}), .gt(Sign));  // open: eq, lt
  Multiplexer #(.width(32), .enable("false")) multiplexer_10 (
    .in0(Out), .in1(and_2_out), .out(multiplexer_10_out), .sel(Select[3]));
  Comparator #(.width(32)) comparator_4 (.a(multiplexer_10_out), .b({32{1'b0}}), .eq(Zero));  // open: gt, lt

  assign IsMult = Select[3];

  // Other names for the same wires on the sheet: Selector[2:0] = Select[2:0]

  // Notes on the sheet:
  //   Input Zone
  //   Math Operations
  //   Logic Operations
  //   Comparison
endmodule

module MULU (
  input  [31:0] A,
  input  [31:0] B,
  output [31:0] Lo,
  output [31:0] Hi
);

  wire Carry_Correction;
  wire [31:0] A_Correction, AxB_Hi, B_Correction, Total_Correction;

  Multiplexer #(.width(32), .enable("false")) multiplexer_1 (
    .in0({32{1'b0}}), .in1(B), .out(A_Correction), .sel(A[31]));
  Multiplexer #(.width(32), .enable("false")) multiplexer_2 (
    .in0({32{1'b0}}), .in1(A), .out(B_Correction), .sel(B[31]));
  Multiplier #(.width(32)) multiplier_1 (.a(A), .b(B), .out(Lo), .cout(AxB_Hi));  // open: cin
  Adder #(.width(32)) adder_1 (
    .a(A_Correction), .b(B_Correction), .out(Total_Correction), .cout(Carry_Correction));  // open: cin
  Adder #(.width(32)) adder_2 (.a(AxB_Hi), .b(Total_Correction), .out(Hi), .cin(Carry_Correction));  // open: cout

  // Notes on the sheet:
  //   Input
  //   Correcciones Iniciales
  //   Demostracion Matematica
  //   Signed A = A - A[31]*2^32
  //   Signed B = B - B[31]*2^32
  //   A*B - A*B[31]*2^32 - B*A[31]*2^32
  //   si y solo si eliminamos los otros terminos sumandoselos
  //   Distribuyendo y teniendo en cuenta el overflow obtenemos que el producto signed es:
  //   por tanto 
  //   Output Zone
  //   usigned = A*B
endmodule

module DIVU (
  input  [31:0] A,
  input  [31:0] B,
  output [31:0] Result,
  output [31:0] Remainder
);

  wire comparator_1_lt, comparator_2_lt;
  wire [1:0] bit_extender_2_out, bit_extender_3_out, bit_extender_4_out, bit_extender_5_out, or_1_out,
       or_2_out, shifter_1_out, shifter_2_out;
  wire [31:0] A_prime, multiplier_1_out, multiplier_2_out, q1, q_1, q_2, qF, r1, r3, r_1, r_2, Rem, Res, rF;

  Divider #(.width(32)) divider_1 (.a(A), .b(B), .out(q1), .rem(r1));  // open: upper
  Subtractor #(.width(32)) subtractor_1 (.a(A), .b(B), .out(r3));  // open: bin, bout
  assign A_prime = {{1{1'b0}}, A[30:0]};  // Bit_Extender bit_extender_1
  Divider #(.width(32)) divider_2 (.a(32'h40000000), .b(B), .out(q_1), .rem(r_1));  // open: upper
  Divider #(.width(32)) divider_3 (.a(A_prime), .b(B), .out(q_2), .rem(r_2));  // open: upper
  Multiplier #(.width(32)) multiplier_1 (.a(32'h2), .b(q_1), .out(multiplier_1_out));  // open: cin, cout
  Multiplier #(.width(32)) multiplier_2 (.a(32'h2), .b(r_1), .out(multiplier_2_out));  // open: cin, cout
  Adder #(.width(32)) adder_1 (.a(multiplier_1_out), .b(q_2), .out(qF));  // open: cin, cout
  Adder #(.width(32)) adder_2 (.a(multiplier_2_out), .b(r_2), .out(rF));  // open: cin, cout
  assign bit_extender_2_out = {{1{1'b0}}, A[31]};  // Bit_Extender bit_extender_2
  assign bit_extender_3_out = {{1{1'b0}}, A[31]};  // Bit_Extender bit_extender_3
  Multiplexer #(.select(2), .width(32), .enable("false")) multiplexer_1 (
    .in0(q1), .in1({32{1'b0}}), .in2(qF), .in3(32'h1), .out(Res), .sel(or_1_out));
  assign or_1_out = shifter_1_out | bit_extender_4_out;  // OR_Gate or_1, 2 bits wide
  assign bit_extender_4_out = {{1{1'b0}}, B[31]};  // Bit_Extender bit_extender_4
  Shifter #(.width(2)) shifter_1 (.in(bit_extender_2_out), .\dist (1'b1), .out(shifter_1_out));
  Multiplexer #(.select(2), .width(32), .enable("false")) multiplexer_2 (
    .in0(r1), .in1(A), .in2(rF), .in3(r3), .out(Rem), .sel(or_2_out));
  assign or_2_out = shifter_2_out | bit_extender_5_out;  // OR_Gate or_2, 2 bits wide
  assign bit_extender_5_out = {{1{1'b0}}, B[31]};  // Bit_Extender bit_extender_5
  Shifter #(.width(2)) shifter_2 (.in(bit_extender_3_out), .\dist (1'b1), .out(shifter_2_out));
  Comparator #(.width(32), .mode("unsigned")) comparator_1 (.a(A), .b(B), .lt(comparator_1_lt));  // open: gt, eq
  Comparator #(.width(32), .mode("unsigned")) comparator_2 (.a(A), .b(B), .lt(comparator_2_lt));  // open: gt, eq
  Multiplexer #(.width(32), .enable("false")) multiplexer_3 (
    .in0(Res), .in1({32{1'b0}}), .out(Result), .sel(comparator_1_lt));
  Multiplexer #(.width(32), .enable("false")) multiplexer_4 (
    .in0(Rem), .in1(A), .out(Remainder), .sel(comparator_2_lt));

  // Other names for the same wires on the sheet: S2 = B[31]; r2[31:0] = A; S1 = A[31]

  // Notes on the sheet:
  //   Caso 00:
  //   Caso 00
  //   Caso 01
  //   Caso 11
  //   Resolvemos la division por una diferencia de casos segun A[31] y B[31]
  //   Como ambos son positivos la division normal basta
  //   caso 01 como A < B siempre entonces solo existe la descomposicion A = 0*B + A
  //   caso 10: Usemos la idea de descomponer A tal que queda 2* 2^30/B + A[30,0]/B
  //   Todo Bajo la premisa A > B
  //   Caso 10
  //   caso 11: Como ambos son demasiado grandes =>  A = B*1 + A - B
endmodule

// ABS
module ABS_Value (
  input  [31:0] A,
  output [31:0] Output
);

  wire comparator_1_lt;
  wire [31:0] minus_A;

  Negator #(.width(32)) negator_1 (.in(A), .out(minus_A));
  Comparator #(.width(32)) comparator_1 (.a({32{1'b0}}), .b(A), .lt(comparator_1_lt));  // open: gt, eq
  Multiplexer #(.width(32), .enable("false")) multiplexer_1 (
    .in0(A), .in1(minus_A), .out(Output), .sel(comparator_1_lt));

  // Other names for the same wires on the sheet: out[31:0] = Output

  // Notes on the sheet:
  //   Input
  //   Absolute
  //   output
endmodule

module Instruction_Decoder (
  input  [31:0] Instruction,
  output [15:0] Constant,
  output [25:0] Destine,
  output [4:0] RS,
  output [4:0] RT,
  output [4:0] RD,
  output [3:0] ALU_Selector,
  output ADDI,
  output ANDI,
  output ORI,
  output XORI,
  output BLTZ,
  output BEQ,
  output BNE,
  output BLEZ,
  output BGTZ,
  output SLTI,
  output SLTIU,
  output LW,
  output SW,
  output WrHL,
  output Wr,
  output IsALU,
  output Jump,
  output push,
  output pop,
  output mfhi,
  output mflo,
  output jr,
  output nop,
  output halt,
  output tty,
  output rnd,
  output kbd
);

  wire or_1_out;
  wire [3:0] ALU_OP, multiplexer_1_out;
  wire [5:0] Func, Op;

  Instruction_Splitter instruction_splitter_1 (
    .Instruction(Instruction), .FUNC_CODE(Func), .OP_CODE(Op), .Destine(Destine), .Constant(Constant),
    .RD(RD), .RT(RT), .RS(RS));
  Instructions_Control_Flags instructions_control_flags_1 (
    .OPCode(Op), .FuncCode(Func), .ALU(ALU_OP), .IsAlu(IsALU), .WriteEnable(Wr), .Write_Hi_Lo_Enable(WrHL),
    .JUMP(Jump), .ADDI(ADDI), .ANDI(ANDI), .ORI(ORI), .XORI(XORI), .BLTZ(BLTZ), .BEQ(BEQ), .BNE(BNE),
    .BLEZ(BLEZ), .BGTZ(BGTZ), .SLTI(SLTI), .SLTIU(SLTIU), .LW(LW), .SW(SW), .Push(push), .Pop(pop),
    .mfhi(mfhi), .mflo(mflo), .nop(nop), .jr(jr), .halt(halt), .tty(tty), .rnd(rnd), .kbd(kbd));
  Multiplexer #(.width(4), .enable("false")) multiplexer_1 (
    .in0(ALU_OP), .in1(4'b0010), .out(multiplexer_1_out), .sel(or_1_out));
  or or_1 (or_1_out, BLTZ, BEQ, BLEZ, BNE, BGTZ);
  Multiplexer #(.width(4), .enable("false")) multiplexer_2 (
    .in0(multiplexer_1_out), .in1(ALU_OP), .out(ALU_Selector), .sel(IsALU));

  // Other names for the same wires on the sheet: ALU[3:0] = ALU_Selector

  // Notes on the sheet:
  //   output
endmodule

module Instruction_Splitter (
  input  [31:0] Instruction,
  output [5:0] FUNC_CODE,
  output [5:0] OP_CODE,
  output [25:0] Destine,
  output [15:0] Constant,
  output [4:0] RD,
  output [4:0] RT,
  output [4:0] RS
);


  assign Constant = Instruction[15:0];
  assign Destine = Instruction[25:0];
  assign FUNC_CODE = Instruction[5:0];
  assign OP_CODE = Instruction[31:26];
  assign RD = Instruction[15:11];
  assign RS = Instruction[25:21];
  assign RT = Instruction[20:16];

  // Other names for the same wires on the sheet: Jump[25:0] = Instruction[25:0]

  // Notes on the sheet:
  //   Decode
  //   Output
endmodule

module Instructions_Control_Flags (
  input  [5:0] OPCode,
  input  [5:0] FuncCode,
  output [3:0] ALU,
  output IsAlu,
  output WriteEnable,
  output Write_Hi_Lo_Enable,
  output JUMP,
  output ADDI,
  output ANDI,
  output ORI,
  output XORI,
  output BLTZ,
  output BEQ,
  output BNE,
  output BLEZ,
  output BGTZ,
  output SLTI,
  output SLTIU,
  output LW,
  output SW,
  output Push,
  output Pop,
  output mfhi,
  output mflo,
  output nop,
  output jr,
  output halt,
  output tty,
  output rnd,
  output kbd
);

  wire ADDI_t, and_5_out, and_11_out, and_12_out, ANDI_t, BEQ_t, BGTZ_t, BLEZ_t, BLTZ_t, BNE_t,
       comparator_1_eq, comparator_2_eq, comparator_3_eq, comparator_5_eq, comparator_12_eq,
       comparator_13_eq, comparator_16_eq, comparator_17_eq, comparator_18_eq, comparator_19_eq,
       comparator_21_eq, comparator_22_eq, comparator_23_eq, comparator_24_eq, is000xxx, is001xxx, is10xxxx,
       is100xxx, is0110xx, is1010xx, LW_t, mem_reg_func1, mem_reg_func2, mem_reg_op, or_1_out, ORI_t, SLTI_t,
       SLTIU_t, special, SW_t, Type_I, Type_R, XORI_t;
  wire [3:0] ALU_op;

  Comparator #(.width(3), .mode("unsigned")) comparator_1 (
    .a(FuncCode[2:0]), .b(3'b011), .eq(comparator_1_eq));  // open: gt, lt
  Comparator #(.width(3), .mode("unsigned")) comparator_2 (
    .a(FuncCode[2:0]), .b(3'b001), .eq(comparator_2_eq));  // open: gt, lt
  Comparator #(.width(3), .mode("unsigned")) comparator_3 (
    .a(FuncCode[5:3]), .b(3'b100), .eq(comparator_3_eq));  // open: gt, lt
  Comparator #(.width(4), .mode("unsigned")) comparator_4 (
    .a(FuncCode[5:2]), .b(4'b0110), .eq(is0110xx));  // open: gt, lt
  Comparator #(.width(4), .mode("unsigned")) comparator_5 (
    .a(FuncCode[5:2]), .b(4'b1010), .eq(comparator_5_eq));  // open: gt, lt
  Comparator #(.width(3), .mode("unsigned")) comparator_6 (.a(OPCode[5:3]), .b(3'b001), .eq(is001xxx));  // open: gt, lt
  Comparator #(.width(3), .mode("unsigned")) comparator_7 (.a(OPCode[5:3]), .b(3'b000), .eq(is000xxx));  // open: gt, lt
  Comparator #(.width(2), .mode("unsigned")) comparator_8 (.a(OPCode[5:4]), .b(2'b10), .eq(is10xxxx));  // open: gt, lt
  Comparator #(.width(6), .mode("unsigned")) comparator_9 (.a(OPCode), .b(6'b111000), .eq(mem_reg_op));  // open: gt, lt
  Comparator #(.width(6), .mode("unsigned")) comparator_10 (
    .a(FuncCode), .b(6'b000001), .eq(mem_reg_func1));  // open: gt, lt
  Comparator #(.width(6), .mode("unsigned")) comparator_11 (
    .a(FuncCode), .b({6{1'b0}}), .eq(mem_reg_func2));  // open: gt, lt
  Comparator #(.width(2)) comparator_12 (.a(FuncCode[1:0]), .b(2'b00), .eq(comparator_12_eq));  // open: gt, lt
  Comparator #(.width(2)) comparator_13 (.a(FuncCode[1:0]), .b(2'b01), .eq(comparator_13_eq));  // open: gt, lt
  Comparator #(.width(6), .mode("unsigned")) comparator_14 (.a(OPCode), .b({6{1'b0}}), .eq(Type_R));  // open: gt, lt
  Comparator #(.width(6), .mode("unsigned")) comparator_15 (.a(OPCode), .b(6'b000010), .eq(JUMP));  // open: gt, lt
  nor nor_1 (Type_I, Type_R, JUMP);
  and and_1 (is100xxx, comparator_3_eq, ~comparator_1_eq, ~comparator_2_eq);  // AND_Gate
  and and_2 (is1010xx, ~comparator_12_eq, comparator_5_eq, ~comparator_13_eq);  // AND_Gate
  Demultiplexer #(.select(3), .enable("false")) demultiplexer_1 (
    .out0(ADDI_t), .out2(SLTI_t), .out3(SLTIU_t), .out4(ANDI_t), .out5(ORI_t), .out6(XORI_t), .in(Type_I),
    .sel(OPCode[2:0]));  // open: out1, out7
  and and_3 (Push, mem_reg_op, mem_reg_func1);
  and and_4 (Pop, mem_reg_op, mem_reg_func2);
  or or_1 (or_1_out, is100xxx, is0110xx, is1010xx);
  Multiplexer #(.select(3), .width(4)) multiplexer_1 (
    .in0(4'b0000), .in2(4'b0001), .in4(4'b0010), .in5(4'b0011), .in6(4'b0100), .in7(4'b0101), .out(ALU_op),
    .sel(FuncCode[2:0]), .en(and_5_out));  // open: in1, in3
  and and_5 (and_5_out, is100xxx, IsAlu);
  and and_6 (IsAlu, or_1_out, Type_R);
  Demultiplexer #(.select(3), .enable("false")) demultiplexer_2 (
    .out1(BLTZ_t), .out4(BEQ_t), .out5(BNE_t), .out6(BLEZ_t), .out7(BGTZ_t), .in(Type_I), .sel(OPCode[2:0]));  // open: out0, out2, out3
  Comparator #(.width(6), .mode("unsigned")) comparator_16 (
    .a(FuncCode), .b(6'b010000), .eq(comparator_16_eq));  // open: gt, lt
  Comparator #(.width(6), .mode("unsigned")) comparator_17 (
    .a(FuncCode), .b(6'b010010), .eq(comparator_17_eq));  // open: gt, lt
  Comparator #(.width(6), .mode("unsigned")) comparator_18 (
    .a(FuncCode), .b({6{1'b0}}), .eq(comparator_18_eq));  // open: gt, lt
  Comparator #(.width(6), .mode("unsigned")) comparator_19 (
    .a(FuncCode), .b(6'b001000), .eq(comparator_19_eq));  // open: gt, lt
  and and_7 (mfhi, comparator_16_eq, Type_R);
  and and_8 (mflo, comparator_17_eq, Type_R);
  and and_9 (nop, comparator_18_eq, Type_R);
  and and_10 (jr, comparator_19_eq, Type_R);
  Multiplexer #(.select(2), .width(4)) multiplexer_2 (
    .in2(4'b0110), .in3(4'b0111), .out(ALU_op), .sel(FuncCode[1:0]), .en(and_11_out));  // open: in0, in1
  and and_11 (and_11_out, is1010xx, IsAlu);
  and and_12 (and_12_out, IsAlu, ~Write_Hi_Lo_Enable);  // AND_Gate
  Multiplexer #(.width(4), .enable("false")) multiplexer_3 (.in0(4'b1100), .in1(ALU_op), .out(ALU), .sel(IsAlu));
  Demultiplexer #(.select(4), .enable("false")) demultiplexer_3 (
    .out3(LW_t), .out11(SW_t), .in(Type_I), .sel(OPCode[3:0]));  // open: out0, out1, out2, out4, out5, out6, out7, out8, out9, out10, out12, out13, out14, out15
  or or_2 (WriteEnable, and_12_out, is001xxx);
  Comparator #(.width(6), .mode("unsigned")) comparator_20 (.a(OPCode), .b({6{1'b1}}), .eq(special));  // open: gt, lt
  Comparator #(.width(6), .mode("unsigned")) comparator_21 (
    .a(FuncCode), .b({6{1'b1}}), .eq(comparator_21_eq));  // open: gt, lt
  Comparator #(.width(6), .mode("unsigned")) comparator_22 (
    .a(FuncCode), .b(6'b000001), .eq(comparator_22_eq));  // open: gt, lt
  Comparator #(.width(6), .mode("unsigned")) comparator_23 (
    .a(FuncCode), .b(6'b000010), .eq(comparator_23_eq));  // open: gt, lt
  Comparator #(.width(6), .mode("unsigned")) comparator_24 (
    .a(FuncCode), .b(6'b000100), .eq(comparator_24_eq));  // open: gt, lt
  Multiplexer #(.select(2), .width(4)) multiplexer_4 (
    .in0(4'b1000), .in1(4'b1001), .in2(4'b1010), .in3(4'b1011), .out(ALU_op), .sel(FuncCode[1:0]),
    .en(Write_Hi_Lo_Enable));
  and and_13 (Write_Hi_Lo_Enable, is0110xx, IsAlu);
  and and_14 (halt, comparator_21_eq, special);
  and and_15 (tty, comparator_22_eq, special);
  and and_16 (rnd, comparator_23_eq, special);
  and and_17 (kbd, comparator_24_eq, special);
  and and_18 (LW, LW_t, is10xxxx);
  and and_19 (SW, SW_t, is10xxxx);
  and and_20 (ADDI, ADDI_t, is001xxx);
  and and_21 (ANDI, ANDI_t, is001xxx);
  and and_22 (ORI, ORI_t, is001xxx);
  and and_23 (XORI, XORI_t, is001xxx);
  and and_24 (BLTZ, BLTZ_t, is000xxx);
  and and_25 (BEQ, BEQ_t, is000xxx);
  and and_26 (BNE, BNE_t, is000xxx);
  and and_27 (BLEZ, BLEZ_t, is000xxx);
  and and_28 (BGTZ, BGTZ_t, is000xxx);
  and and_29 (SLTI, SLTI_t, is001xxx);
  and and_30 (SLTIU, SLTIU_t, is001xxx);

  // Other names for the same wires on the sheet: _100xxx[2:0] = FuncCode[2:0]; _0110xx[1:0] = FuncCode[1:0];
  //   _1010xx[1:0] = FuncCode[1:0]; Func[5:0] = FuncCode; IsAluOP = IsAlu; _000xxx[2:0] = OPCode[2:0];
  //   _001xxx[2:0] = OPCode[2:0]; _10xxxx[3:0] = OPCode[3:0]; OP[5:0] = OPCode; Type_J = JUMP; Write = WriteEnable;
  //   WriteHiLo = Write_Hi_Lo_Enable

  // Notes on the sheet:
  //   Input Zone
  //   Stack
  //   Type I
  //   Is ALU Operation?
  //   Select Type Operation
  //   Type R
  //   Select Alu operator
  //   Write Enable
  //   especiales
  //   Output Zone
endmodule

module Instruction_Register (
  input  [31:0] Instruction,
  input  Enable,
  input  RST,
  input  Clk,
  output [31:0] Instruction_2
);

  Register #(.width(32)) u_Instruction (.D(Instruction), .en(Enable), .Q(Instruction_2), .clk(Clk), .clr(RST));
endmodule

module Register_File (
  input  [31:0] DataIncome,
  input  [4:0] DataAddress,
  input  [4:0] Selector_A,
  input  [4:0] Selector_B,
  input  [31:0] Hi_in,
  input  [31:0] Lo_in,
  input  Reset,
  input  Clock,
  input  in_9,
  input  WriteEnable,
  output [31:0] OutA,
  output [31:0] OutB,
  output [31:0] Hi_out,
  output [31:0] Lo_out,
  output [31:0] SP
);

  wire Dir1, Dir2, Dir3, Dir4, Dir5, Dir6, Dir7, Dir8, Dir9, Dir10, Dir11, Dir12, Dir13, Dir14, Dir15, Dir16,
       Dir17, Dir18, Dir19, Dir20, Dir21, Dir22, Dir23, Dir24, Dir25, Dir26, Dir27, Dir28, Dir29, Dir30,
       DirSP;
  wire [31:0] out1, out2, out3, out4, out5, out6, out7, out8, out9, out10, out11, out12, out13, out14, out15,
       out16, out17, out18, out19, out20, out21, out22, out23, out24, out25, out26, out27, out28, out29,
       out30;

  Decoder #(.select(5), .disabled(0)) decoder_1 (
    .out1(Dir1), .out2(Dir2), .out3(Dir3), .out4(Dir4), .out5(Dir5), .out6(Dir6), .out7(Dir7), .out8(Dir8),
    .out9(Dir9), .out10(Dir10), .out11(Dir11), .out12(Dir12), .out13(Dir13), .out14(Dir14), .out15(Dir15),
    .out16(Dir16), .out17(Dir17), .out18(Dir18), .out19(Dir19), .out20(Dir20), .out21(Dir21), .out22(Dir22),
    .out23(Dir23), .out24(Dir24), .out25(Dir25), .out26(Dir26), .out27(Dir27), .out28(Dir28), .out29(Dir29),
    .out30(Dir30), .out31(DirSP), .sel(DataAddress), .en(WriteEnable));  // open: out0
  Register #(.width(32)) register_1 (.D(DataIncome), .en(Dir8), .Q(out8), .clk(Clock), .clr(Reset));
  Register #(.width(32)) register_2 (.D(DataIncome), .en(Dir16), .Q(out16), .clk(Clock), .clr(Reset));
  Register #(.width(32)) register_3 (.D(DataIncome), .en(Dir24), .Q(out24), .clk(Clock), .clr(Reset));
  Register #(.width(32)) register_4 (.D(DataIncome), .en(Dir1), .Q(out1), .clk(Clock), .clr(Reset));
  Register #(.width(32)) register_5 (.D(DataIncome), .en(Dir9), .Q(out9), .clk(Clock), .clr(Reset));
  Register #(.width(32)) register_6 (.D(DataIncome), .en(Dir17), .Q(out17), .clk(Clock), .clr(Reset));
  Register #(.width(32)) register_7 (.D(DataIncome), .en(Dir25), .Q(out25), .clk(Clock), .clr(Reset));
  Register #(.width(32)) register_8 (.D(DataIncome), .en(Dir2), .Q(out2), .clk(Clock), .clr(Reset));
  Register #(.width(32)) register_9 (.D(DataIncome), .en(Dir10), .Q(out10), .clk(Clock), .clr(Reset));
  Register #(.width(32)) register_10 (.D(DataIncome), .en(Dir18), .Q(out18), .clk(Clock), .clr(Reset));
  Register #(.width(32)) register_11 (.D(DataIncome), .en(Dir26), .Q(out26), .clk(Clock), .clr(Reset));
  Multiplexer #(.select(5), .width(32), .enable("false")) multiplexer_1 (
    .in0({32{1'b0}}), .in1(out1), .in2(out2), .in3(out3), .in4(out4), .in5(out5), .in6(out6), .in7(out7),
    .in8(out8), .in9(out9), .in10(out10), .in11(out11), .in12(out12), .in13(out13), .in14(out14),
    .in15(out15), .in16(out16), .in17(out17), .in18(out18), .in19(out19), .in20(out20), .in21(out21),
    .in22(out22), .in23(out23), .in24(out24), .in25(out25), .in26(out26), .in27(out27), .in28(out28),
    .in29(out29), .in30(out30), .in31(SP), .out(OutA), .sel(Selector_A));
  Register #(.width(32)) register_12 (.D(DataIncome), .en(Dir3), .Q(out3), .clk(Clock), .clr(Reset));
  Register #(.width(32)) register_13 (.D(DataIncome), .en(Dir11), .Q(out11), .clk(Clock), .clr(Reset));
  Register #(.width(32)) register_14 (.D(DataIncome), .en(Dir19), .Q(out19), .clk(Clock), .clr(Reset));
  Register #(.width(32)) register_15 (.D(DataIncome), .en(Dir27), .Q(out27), .clk(Clock), .clr(Reset));
  Register #(.width(32)) register_16 (.D(DataIncome), .en(Dir4), .Q(out4), .clk(Clock), .clr(Reset));
  Register #(.width(32)) register_17 (.D(DataIncome), .en(Dir12), .Q(out12), .clk(Clock), .clr(Reset));
  Register #(.width(32)) register_18 (.D(DataIncome), .en(Dir20), .Q(out20), .clk(Clock), .clr(Reset));
  Register #(.width(32)) register_19 (.D(DataIncome), .en(Dir28), .Q(out28), .clk(Clock), .clr(Reset));
  Multiplexer #(.select(5), .width(32), .enable("false")) multiplexer_2 (
    .in0({32{1'b0}}), .in1(out1), .in2(out2), .in3(out3), .in4(out4), .in5(out5), .in6(out6), .in7(out7),
    .in8(out8), .in9(out9), .in10(out10), .in11(out11), .in12(out12), .in13(out13), .in14(out14),
    .in15(out15), .in16(out16), .in17(out17), .in18(out18), .in19(out19), .in20(out20), .in21(out21),
    .in22(out22), .in23(out23), .in24(out24), .in25(out25), .in26(out26), .in27(out27), .in28(out28),
    .in29(out29), .in30(out30), .in31(SP), .out(OutB), .sel(Selector_B));
  Register #(.width(32)) register_20 (.D(DataIncome), .en(Dir5), .Q(out5), .clk(Clock), .clr(Reset));
  Register #(.width(32)) register_21 (.D(DataIncome), .en(Dir13), .Q(out13), .clk(Clock), .clr(Reset));
  Register #(.width(32)) register_22 (.D(DataIncome), .en(Dir21), .Q(out21), .clk(Clock), .clr(Reset));
  Register #(.width(32)) register_23 (.D(DataIncome), .en(Dir29), .Q(out29), .clk(Clock), .clr(Reset));
  Register #(.width(32)) register_24 (.D(DataIncome), .en(Dir6), .Q(out6), .clk(Clock), .clr(Reset));
  Register #(.width(32)) register_25 (.D(DataIncome), .en(Dir14), .Q(out14), .clk(Clock), .clr(Reset));
  Register #(.width(32)) register_26 (.D(DataIncome), .en(Dir22), .Q(out22), .clk(Clock), .clr(Reset));
  Register #(.width(32)) register_27 (.D(DataIncome), .en(Dir30), .Q(out30), .clk(Clock), .clr(Reset));
  Register #(.width(32)) register_28 (.D(DataIncome), .en(Dir7), .Q(out7), .clk(Clock), .clr(Reset));
  Register #(.width(32)) register_29 (.D(DataIncome), .en(Dir15), .Q(out15), .clk(Clock), .clr(Reset));
  Register #(.width(32)) register_30 (.D(DataIncome), .en(Dir23), .Q(out23), .clk(Clock), .clr(Reset));
  Register #(.width(32)) register_31 (.D(DataIncome), .en(DirSP), .Q(SP), .clk(Clock), .clr(Reset));
  Register #(.width(32)) register_32 (.D(Hi_in), .en(in_9), .Q(Hi_out), .clk(Clock), .clr(Reset));
  Register #(.width(32)) register_33 (.D(Lo_in), .en(in_9), .Q(Lo_out), .clk(Clock), .clr(Reset));

  // Other names for the same wires on the sheet: Clk = Clock; DA[4:0] = DataAddress; DataInc[31:0] = DataIncome;
  //   DHi[31:0] = Hi_in; DLo[31:0] = Lo_in; outHi[31:0] = Hi_out; outLo[31:0] = Lo_out; outSP[31:0] = SP; RST = Reset;
  //   SelectA[4:0] = Selector_A; SelectB[4:0] = Selector_B; WEnable = WriteEnable; WriteHiLo = in_9

  // Notes on the sheet:
  //   Register Input
  //   Configuration Inputs
  //   Registers
  //   WRITE
  //   READ
  //   Hi Lo Registers
  //   Hi
  //   Lo
  //   Output Zone
endmodule

module Memory_Control (
  input  [3:0] in_1,
  input  [3:0] in_2,
  input  in_3,
  input  in_4,
  input  [31:0] in_5,
  input  in_6,
  input  in_7,
  input  in_8,
  input  in_9,
  input  [31:0] in_10,
  input  [31:0] in_11,
  input  [31:0] in_12,
  input  [31:0] in_13,
  output [31:0] Output,
  output [31:0] Output_2,
  output [31:0] Output_3,
  output [31:0] Output_4,
  output [15:0] Output_5,
  output [3:0] Output_6,
  output Output_7,
  output Output_8,
  output Output_9,
  output Output_10,
  output Output_11
);

  wire CSD, CSI, or_1_out, stop;
  wire [31:0] DO0, DO1, DO2, DO3, IO0, IO1, IO2, IO3;

  or or_1 (or_1_out, in_6, stop);
  RAM_Read ram_read_1 (
    .in_5(in_5), .in_6(in_10), .in_7(in_11), .in_8(in_12), .in_1(in_1), .in_3(in_4), .in_4(in_7),
    .Output_3(IO0), .Output_4(IO1), .Output_5(IO2), .Output_6(IO3), .Output(CSI), .Output_2(Output_9),
    .in_2(in_3));
  D_Flip_Flop #(.trigger("falling")) d_ff_1 (
    .clk(in_3), .D(in_6), .Q(Output_8), .en(or_1_out));  // open: Qn, preset, reset
  Delay delay_1 (.in_1(Output_8), .in_2(Output_11), .in_3(in_3), .in_4(in_2), .Output(stop));
  Multiplexer #(.width(32), .enable("false")) multiplexer_1 (
    .in0({DO0[7:0], DO0[15:8], DO0[23:16], DO0[31:24]}), .in1(IO0), .out(Output), .sel(in_9));
  Multiplexer #(.width(32), .enable("false")) multiplexer_2 (
    .in0({DO2[7:0], DO2[15:8], DO2[23:16], DO2[31:24]}), .in1(IO2), .out(Output_3), .sel(in_9));
  RAM_Read ram_read_2 (
    .in_5(in_5), .in_6(in_10), .in_7(in_11), .in_8(in_12), .in_1(in_1), .in_3(in_4), .in_4(in_8),
    .Output_3(DO0), .Output_4(DO1), .Output_5(DO2), .Output_6(DO3), .Output(CSD), .Output_2(Output_10),
    .in_2(in_3));
  D_Flip_Flop #(.trigger("falling")) d_ff_2 (.clk(in_3), .D(stop), .Q(Output_11));  // open: Qn, preset, en, reset
  Multiplexer #(.width(32), .enable("false")) multiplexer_3 (
    .in0({DO1[7:0], DO1[15:8], DO1[23:16], DO1[31:24]}), .in1(IO1), .out(Output_2), .sel(in_9));
  Multiplexer #(.width(32), .enable("false")) multiplexer_4 (
    .in0({DO3[7:0], DO3[15:8], DO3[23:16], DO3[31:24]}), .in1(IO3), .out(Output_4), .sel(in_9));
  Demultiplexer #(.select(2), .enable("false")) demultiplexer_1 (
    .out0(Output_6[0]), .out1(Output_6[1]), .out2(Output_6[2]), .out3(Output_6[3]), .in(1'b1),
    .sel(in_13[3:2]));
  or or_2 (Output_7, CSD, CSI, Output_8);

  assign Output_5 = in_13[19:4];

  // Other names for the same wires on the sheet: bank0[31:0] = in_5; bank1[31:0] = in_10; bank2[31:0] = in_11;
  //   bank3[31:0] = in_12; clock = in_3; CS = Output_7; DP_address[31:0] = in_13; ADDR[15:0] = in_13[19:4];
  //   get_data = in_8; get_inst = in_7; is_inst = in_9; MASK[3:0] = Output_6; out_bank0[31:0] = Output;
  //   out_bank1[31:0] = Output_2; out_bank2[31:0] = Output_3; out_bank3[31:0] = Output_4; read_time[3:0] = in_1;
  //   ready_data = Output_10; ready_inst = Output_9; ready_write = Output_11; reset = in_4; RW = Output_8;
  //   write = in_6; write_time[3:0] = in_2
endmodule

module RAM_Read (
  input  [3:0] in_1,
  input  in_2,
  input  in_3,
  input  in_4,
  input  [31:0] in_5,
  input  [31:0] in_6,
  input  [31:0] in_7,
  input  [31:0] in_8,
  output Output,
  output Output_2,
  output [31:0] Output_3,
  output [31:0] Output_4,
  output [31:0] Output_5,
  output [31:0] Output_6
);

  wire a, enable, or_1_out, stop;

  D_Flip_Flop #(.trigger("falling")) d_ff_1 (.clk(in_2), .D(in_4), .Q(a), .en(or_1_out));  // open: Qn, preset, reset
  or or_1 (or_1_out, in_4, stop);
  Delay delay_1 (.in_1(a), .in_2(Output_2), .in_3(in_2), .in_4(in_1), .Output(stop));
  Register #(.width(32)) register_1 (.D(in_5), .en(enable), .Q(Output_3), .clk(in_2), .clr(in_3));
  Register #(.width(32)) register_2 (.D(in_7), .en(enable), .Q(Output_5), .clk(in_2), .clr(in_3));
  or or_2 (Output, a, enable);
  D_Flip_Flop #(.trigger("falling")) d_ff_2 (
    .clk(in_2), .D(stop), .Q(enable), .reset(Output_2));  // open: Qn, preset, en
  Register #(.width(32)) register_3 (.D(in_6), .en(enable), .Q(Output_4), .clk(in_2), .clr(in_3));
  Register #(.width(32)) register_4 (.D(in_8), .en(enable), .Q(Output_6), .clk(in_2), .clr(in_3));
  D_Flip_Flop #(.trigger("falling")) d_ff_3 (.clk(in_2), .D(enable), .Q(Output_2));  // open: Qn, preset, en, reset

  // Other names for the same wires on the sheet: bank0[31:0] = in_5; bank1[31:0] = in_6; bank2[31:0] = in_7;
  //   bank3[31:0] = in_8; chip_select = Output; clock = in_2; get = in_4; out_bank0[31:0] = Output_3;
  //   out_bank1[31:0] = Output_4; out_bank2[31:0] = Output_5; out_bank3[31:0] = Output_6; read_time[3:0] = in_1;
  //   ready = Output_2; reset = in_3
endmodule

module Delay (
  input  in_1,
  input  in_2,
  input  in_3,
  input  [3:0] in_4,
  output Output
);

  wire [3:0] counter_1_q;

  Counter #(.width(4), .max('hf)) counter_1 (
    .count(in_1), .Q(counter_1_q), .clk(in_3), .clr(in_2));  // open: load, D, carry
  Comparator #(.width(4)) comparator_1 (.a(in_4), .b(counter_1_q), .eq(Output));  // open: gt, lt

  // Other names for the same wires on the sheet: clock = in_3; ready = Output; reset = in_2; start = in_1;
  //   wait_time[3:0] = in_4
endmodule
